# Fritzing sketch bloc prog v2 (saved by Fritzing 0.9.2b)
circuit board: 5cm x 4.50072cm
breadboards: 1

parts:
  Composant1 = Arduino Nano (Rev3.0)
  R3 = Resistor [tolerance=±5% resistance=1k package="0402 [SMD]"]
  R4 = Resistor [tolerance=±5% resistance=1k package="0402 [SMD]"]
  R5 = Resistor [tolerance=±5% resistance=1k package="0402 [SMD]"]
  R6 = Resistor [tolerance=±5% resistance=1k package="0402 [SMD]"]
  J2 = double row female pin header, 8 pins [form="♀ (female)"]
  J1 = female pin header, 5 pins [form="♀ (female)"]
  J3 = female pin header, 2 pins [form="♀ (female)"]
  J4 = female pin header, 10 pins [form="♀ (female)"]
  J5 = female pin header, 1 pin [form="♀ (female)"]  # not connected
  J6 = female pin header, 1 pin [form="♀ (female)"]  # not connected
  J7 = female pin header, 1 pin [form="♀ (female)"]  # not connected

nets:
  N1: Composant1.GND, J1.pin2, J1.pin3, J1.pin4, J1.pin5, J3.pin1, J4.pin9, J4.pin10
  N2: Composant1.D3, J4.pin8
  N3: Composant1.D4, J4.pin7
  N4: Composant1.D5, J4.pin6
  N5: Composant1.D6, J4.pin5
  N6: Composant1.D7, J4.pin4
  N7: Composant1.D8, J4.pin3
  N8: Composant1.D9, J4.pin2
  N9: Composant1.D10, J4.pin1
  N10: Composant1.VIN, J3.pin2
  N11: Composant1.5V, R3.Pin_1, R4.Pin_1, R5.Pin_1, R6.Pin_1, J2.pin5, J2.pin6, J2.pin7, J2.pin8
  N12: R3.Pin_0, J2.pin4
  N13: R4.Pin_0, J2.pin3
  N14: R5.Pin_0, J2.pin2
  N15: R6.Pin_0, J2.pin1

notes:
  GND
  RX-IN
  TX-IN
  RX-OUT
  TX-OUT
  CAPT 1
  CAPT 2
  CAPT 3
  CAPT 4
  VIN
  5V
  C1
  C2
  C3
  C4
  BATTERIE
  +
  -
  NANO
