# Fritzing sketch robot3 (saved by Fritzing 0.9.3b)
circuit board: 8cm x 5.99944cm
breadboards: 1

parts:
  Composant1 = Arduino Nano (Rev3.0)
  Composant2 = NRF24L01+ Breakout Board
  J2 = female pin header, 1 pin [form="♀ (female)"]
  J3 = female pin header, 2 pins [form="♀ (female)"]
  J4 = female pin header, 1 pin [form="♀ (female)"]
  J5 = female pin header, 1 pin [form="♀ (female)"]
  J6 = female pin header, 2 pins [form="♀ (female)"]
  J7 = female pin header, 2 pins [form="♀ (female)"]
  J8 = female pin header, 1 pin [form="♀ (female)"]
  R2-1kΩ1 = Resistor [tolerance=±5% resistance=1k package="1206 [SMD]"]
  R2-1kΩ2 = Resistor [tolerance=±5% resistance=1k package="1206 [SMD]"]
  J9 = female pin header, 2 pins [form="♀ (female)"]
  Pololu_A1 = Pololu A4988 [package=SO16]
  Pololu_A2 = Pololu A4988 [package=SO16]
  J10 = female pin header, 4 pins [form="♀ (female)"]
  J11 = female pin header, 4 pins [form="♀ (female)"]
  J12 = female pin header, 2 pins [form="♀ (female)"]
  SG2 = Buzzer 12mm [package=buzzer-12mm-ns-kit]
  J13 = female pin header, 2 pins [form="♀ (female)"]
  J14 = female pin header, 1 pin [form="♀ (female)"]  # not connected
  J15 = female pin header, 1 pin [form="♀ (female)"]  # not connected
  J16 = female pin header, 1 pin [form="♀ (female)"]  # not connected

nets (from the pcb view):
  GND: Composant1.GND, Composant2.GND, J3.pin1, J3.pin2, R2-1kΩ2.Pin_0, Pololu_A1.GND, Pololu_A2.GND, SG2.2
  N1: Composant1.D2, J13.pin1
  N2: Composant1.D6, J5.pin1
  N3: Composant1.D7, Composant2.CE
  N4: Composant1.D8, Composant2.CS
  N5: Composant1.D11/MOSI, Composant2.MOSI
  N6: Composant1.D12/MISO, Composant2.MISO
  N7: Composant1.VIN, J2.pin1
  N8: Composant1.5V, J4.pin1
  N9: Composant1.A7, J12.pin1
  N10: Composant1.A6, Pololu_A1.SLEEP
  N11: Composant1.A5, Pololu_A1.STEP
  N12: Composant1.A4, Pololu_A1.DIR
  N13: Composant1.A2, Pololu_A2.SLEEP
  N14: Composant1.A1, Pololu_A2.STEP
  N15: Composant1.A0, Pololu_A2.DIR
  N16: Composant1.3V3, J7.pin1
  N17: Composant1.D13/SCK, J6.pin1
  N18: Composant2.VCC, J7.pin2
  N19: Composant2.SCK, J6.pin2
  N20: J8.pin1, R2-1kΩ1.Pin_1
  N21: R2-1kΩ1.Pin_0, R2-1kΩ2.Pin_1, J12.pin2
  N22: J9.pin2, Pololu_A1.VMOT, Pololu_A2.VMOT
  N23: Pololu_A1.1B, J10.pin1
  N24: Pololu_A1.1A, J10.pin2
  N25: Pololu_A1.2A, J10.pin3
  N26: Pololu_A1.2B, J10.pin4
  N27: Pololu_A2.1B, J11.pin1
  N28: Pololu_A2.1A, J11.pin2
  N29: Pololu_A2.2A, J11.pin3
  N30: Pololu_A2.2B, J11.pin4
  N31: SG2.1, J13.pin2

notes:
  NANO
  RADIO
  BATTERIE
  +
  -
  GND
  5V
  B2
  B1
  A1
  A2
  R2-1kΩ2
  R1-1kΩ2
  DRIVER DROIT
  DRIVER GAUCHE
  GDIR 0
  DDIR 4
  DSTEP 5
  GSTEP 1
  GSLEEP 2
  DSLEEP 6
  NEO
  D0
  BUZZER
